# Fritzing sketch bracelet (saved by Fritzing 0.9.3b)

parts:
  Part1 = Arduino Uno (Rev3)
  Part2 = Bluetooth HC-05 Macho
  Part3 = Adafruit PN532 Breakout [part_number="Adafruit #364"]
  R1 = Resistor [tolerance=±5% resistance=100 package=THT]
  J1 = Piezo Speaker
  LED1 = LED - 5mm [color="Red (633nm)" package="5 mm [THT]"]
  LED2 = LED - 5mm [color="Yellow (595nm)" package="5 mm [THT]"]
  R2 = Resistor [tolerance=±5% resistance=220 package=THT]

nets:
  N1: Part1.D9_PWM, R1.Pin_0
  N2: Part1.D10_PWM/SS, Part3.NSS/SCL/RX
  N3: Part1.D11_PWM/MOSI, Part3.MOSI/SDA/TX
  N4: Part1.D12/MISO, Part3.MISO
  N5: Part1.D13/SCK, Part3.SCK
  N6: Part1.D2, Part2.TXD
  N7: Part1.D3_PWM, Part2.RXD
  N8: Part1.D4, LED1.anode
  N9: Part1.D5_PWM, LED2.anode
  5V: Part1.5V, Part2.VCC
  GND: Part1.GND, Part2.GND
  N10: Part3.GND, J1.pin1, R2.Pin_0
  N11: R1.Pin_1, J1.pin2
  N12: LED1.cathode, LED2.cathode, R2.Pin_1

custom parts:
  Adafruit PN532 Breakout: The PN532 is the most popular NFC chip, and is what is embedded in pretty much every phone or device that does NFC. It can pretty much do it all, such as read and write to tags and cards, communicate with phones (say for payment processing), and 'act' like a NFC tag. If you want to do any sort of embedded NFC work, this is the chip you'll want to use! NFC (Near Field Communications) is a way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
